# Fritzing sketch sketch (saved by Fritzing 0.7.7b)

parts:
  Arduino1 = Arduino
  J1 = Basic Servo
  X2 = Sonar

nets:
  N1: Arduino1.D13, X2.SCL
  N2: Arduino1.D12, X2.SDA
  +5V: Arduino1.+5V, J1.vcc, X2.+5
  GND: Arduino1.GND, X2.GND

custom parts:
  Sonar: Devantech SRF08 sonar range-finder. I2C interface. Other Devantech sonars similar
